// Logisim project ex.1a.circ as structural Verilog: 2 circuits, main circuit main
module main (
);

  wire and_1_out, clock_1_out, clock_2_out, clock_3_out, clock_4_out, clock_5_out, clock_6_out, or_1_out,
       or_2_out;

  Clock clock_1 (.out(clock_1_out));
  Clock clock_2 (.out(clock_2_out));
  Clock clock_3 (.out(clock_3_out));
  Clock clock_4 (.out(clock_4_out));
  or or_1 (or_1_out, clock_1_out, clock_2_out);
  or or_2 (or_2_out, clock_3_out, clock_4_out);
  Clock clock_5 (.out(clock_5_out));
  Clock clock_6 (.out(clock_6_out));
  and and_1 (and_1_out, or_1_out, clock_5_out, clock_5_out, clock_6_out, or_2_out);
  LED led_1 (.in(and_1_out));
endmodule

module ex1a (
  input  a,
  input  b,
  input  c,
  input  d,
  input  e,
  input  f,
  output s
);

  wire or_1_out, or_2_out;

  or or_1 (or_1_out, a, b);
  or or_2 (or_2_out, d, f);
  and and_1 (s, or_1_out, c, or_2_out, e);
endmodule
