// Logisim project ex.1c.circ as structural Verilog: 2 circuits, main circuit main
module main (
);

  wire clock_1_out, clock_2_out, clock_3_out, clock_4_out, clock_5_out, clock_6_out, or_1_out, or_2_out,
       or_3_out, or_4_out;

  Clock clock_1 (.out(clock_1_out));
  Clock clock_2 (.out(clock_2_out));
  Clock clock_3 (.out(clock_3_out));
  Clock clock_4 (.out(clock_4_out));
  Clock clock_5 (.out(clock_5_out));
  Clock clock_6 (.out(clock_6_out));
  or or_1 (or_1_out, clock_1_out, clock_2_out);
  or or_2 (or_2_out, clock_3_out, clock_4_out);
  or or_3 (or_3_out, clock_5_out, clock_6_out);
  or or_4 (or_4_out, or_1_out, or_2_out, or_3_out);
  LED led_1 (.in(or_4_out));
endmodule

module ex_1c (
  input  a,
  input  b,
  input  c,
  input  d,
  input  e,
  input  f,
  output s
);

  or or_1 (s, a, b, c, d, e, f);
endmodule
