// Logisim project ex.1d.circ as structural Verilog: 2 circuits, main circuit main
module main (
);

  wire and_1_out, and_2_out, and_3_out, clock_1_out, clock_2_out, clock_3_out, clock_4_out, clock_5_out,
       clock_6_out, or_1_out;

  Clock clock_1 (.out(clock_1_out));
  Clock clock_2 (.out(clock_2_out));
  Clock clock_3 (.out(clock_3_out));
  Clock clock_4 (.out(clock_4_out));
  Clock clock_5 (.out(clock_5_out));
  Clock clock_6 (.out(clock_6_out));
  and and_1 (and_1_out, clock_1_out, clock_2_out);
  and and_2 (and_2_out, clock_3_out, clock_4_out);
  and and_3 (and_3_out, clock_5_out, clock_6_out);
  LED led_1 (.in(or_1_out));
  or or_1 (or_1_out, and_1_out, and_2_out, and_3_out);
endmodule

module ex_1d (
  input  a,
  input  b,
  input  c,
  input  d,
  input  e,
  input  f,
  output s
);

  wire and_1_out, and_2_out, and_3_out;

  and and_1 (and_1_out, a, b);
  and and_2 (and_2_out, c, d);
  and and_3 (and_3_out, e, f);
  or or_1 (s, and_1_out, and_2_out, and_3_out);
endmodule
