// Logisim project ex16_prova.circ as structural Verilog
module exercicio16 (
  input  a,
  input  b,
  input  c,
  input  d,
  output s
);

  wire and_1_out, and_2_out, and_3_out, not_1_out, not_2_out, not_3_out;

  not not_1 (not_1_out, b);
  and and_1 (and_1_out, not_1_out, not_2_out);
  not not_2 (not_2_out, d);
  not not_3 (not_3_out, c);
  and and_2 (and_2_out, not_3_out, d);
  and and_3 (and_3_out, a, b, c);
  or or_1 (s, and_1_out, and_2_out, and_3_out);
endmodule

module exercicio_1novo (
  input  a,
  input  b,
  input  c,
  input  d,
  output s
);

  wire and_1_out, and_2_out, and_3_out, not_1_out, not_2_out, not_3_out;

  not not_1 (not_1_out, b);
  and and_1 (and_1_out, not_1_out, not_2_out);
  not not_2 (not_2_out, d);
  not not_3 (not_3_out, c);
  and and_2 (and_2_out, not_3_out, d);
  and and_3 (and_3_out, a, b, c);
  or or_1 (s, and_1_out, and_2_out, and_3_out);
endmodule
