// Logisim project teste_6.circ as structural Verilog: 3 circuits, main circuit main
module main (
  output out_1
);

  wire and_1_out, and_2_out, and_3_out, clock_1_out, clock_2_out, clock_3_out, clock_4_out, clock_5_out,
       clock_6_out, or_1_out;

  Clock clock_1 (.out(clock_1_out));
  Clock clock_2 (.out(clock_2_out));
  Clock clock_3 (.out(clock_3_out));
  Clock clock_4 (.out(clock_4_out));
  Clock clock_5 (.out(clock_5_out));
  Clock clock_6 (.out(clock_6_out));
  and and_1 (and_1_out, clock_1_out, clock_2_out);
  or or_1 (or_1_out, clock_3_out, clock_4_out);
  and and_2 (and_2_out, clock_5_out, clock_6_out);
  and and_3 (and_3_out, or_1_out, and_2_out);
  and and_4 (out_1, and_1_out, and_3_out, and_3_out);
  LED led_1 (.in(out_1));
endmodule

module teste_6 (
  input  a,
  input  b,
  input  c,
  input  d,
  input  e,
  input  f,
  output s
);

  wire or_1_out;

  or or_1 (or_1_out, c, d);
  and and_1 (s, a, b, e, f, or_1_out);
endmodule

module ex1_a (
  input  a,
  input  b,
  input  c,
  input  d,
  input  e,
  input  f,
  output s
);

  wire or_1_out, or_2_out;

  or or_1 (or_1_out, a, b);
  or or_2 (or_2_out, d, f);
  and and_1 (s, or_1_out, c, or_2_out, e);
endmodule
